# Fritzing sketch schema (saved by Fritzing 0.9.6b)

parts:
  Part1 = Arduino Pro Mini v13
  Part2 = InvenSense MPU6050
  BAT1 = Battery Holders [package=battcom_20mm_pth]

nets:
  N1: Part1.A4, Part2.SDA
  N2: Part1.A5, Part2.SCL
  GND: Part1.GND, Part2.GND, BAT1.-
  VCC: Part1.VCC, Part2.VCC, BAT1.+
